// Logisim project HERA.circ as structural Verilog: 16 circuits, main circuit main
module main (
);

  wire clk, enable, LD, ST;
  wire [4:0] F, Flags_out;
  wire [15:0] address, FP_in, FP_out, instruction, PC_OUT, R_1, R_2, R_3, R_13, R_a, R_b, R_d, Ra,
       ram_1_dout, ram_address, RAMOUT, Rb_out;

  Clock u_clk (.out(clk));
  ROM #(.addrWidth(16), .dataWidth(16)) rom_1 (.addr(address), .data(instruction));
  PC pc_1 (.PC_out(PC_OUT), .BR(enable), .clk(clk), .addresss(address));
  Reg_Control reg_control_1 (
    .clk(clk), .instruction(instruction), .Rd(R_d), .Ra_in(Ra), .Rb_in(Rb_out), .FP_in(FP_out), .R_1(R_1),
    .R_2(R_2), .R_3(R_3), .R_13(R_13), .FP_out(FP_in), .R_b(R_b), .R_a(R_a));
  RAM_Instructions ram_instructions_1 (.R_b(R_b), .instruction(instruction), .Address(ram_address), .LD(LD), .ST(ST));
  RAM #(.addrWidth(16), .asyncread("true"), .dataWidth(16)) ram_1 (
    .addr(ram_address), .we(ST), .oe(LD), .clk(clk), .din(R_a), .dout(ram_1_dout));
  DotMatrix #(.dotshape("circle"), .matrixrows(1)) dotmatrix_1 (
    .col0(F[0]), .col1(F[1]), .col2(F[2]), .col3(F[3]), .col4(F[4]));
  ALSU alsu_1 (
    .Flags(Flags_out), .PC_in(address), .R_a(R_a), .R_b(R_b), .Rd(R_d), .FP(FP_in),
    .instruction(instruction), .RAM_out(RAMOUT), .R_d(R_d), .PC_out(PC_OUT), .Rb_out(Rb_out), .Ra_out(Ra),
    .FP_out(FP_out), .enable(enable), .Flags_out(F));
  Multiplexer #(.width(16)) multiplexer_1 (.in0({16{1'b0}}), .in1(ram_1_dout), .out(RAMOUT), .sel(LD));
  FlagBank flagbank_1 (.clk(clk), .flags(F), .flags_out(Flags_out));
  Hex_Digit_Display hex_digit_display_1 (.value(address[15:12]));  // open: dp
  Hex_Digit_Display hex_digit_display_2 (.value(address[11:8]));  // open: dp
  Hex_Digit_Display hex_digit_display_3 (.value(instruction[15:12]));  // open: dp
  Hex_Digit_Display hex_digit_display_4 (.value(instruction[11:8]));  // open: dp
  Hex_Digit_Display hex_digit_display_5 (.value(R_1[15:12]));  // open: dp
  Hex_Digit_Display hex_digit_display_6 (.value(R_1[11:8]));  // open: dp
  Hex_Digit_Display hex_digit_display_7 (.value(R_2[15:12]));  // open: dp
  Hex_Digit_Display hex_digit_display_8 (.value(R_2[11:8]));  // open: dp
  Hex_Digit_Display hex_digit_display_9 (.value(R_3[15:12]));  // open: dp
  Hex_Digit_Display hex_digit_display_10 (.value(R_3[11:8]));  // open: dp
  Hex_Digit_Display hex_digit_display_11 (.value(ram_address[15:12]));  // open: dp
  Hex_Digit_Display hex_digit_display_12 (.value(ram_address[11:8]));  // open: dp
  Hex_Digit_Display hex_digit_display_13 (.value(RAMOUT[15:12]));  // open: dp
  Hex_Digit_Display hex_digit_display_14 (.value(RAMOUT[11:8]));  // open: dp
  Hex_Digit_Display hex_digit_display_15 (.value(address[7:4]));  // open: dp
  Hex_Digit_Display hex_digit_display_16 (.value(instruction[7:4]));  // open: dp
  Hex_Digit_Display hex_digit_display_17 (.value(R_1[7:4]));  // open: dp
  Hex_Digit_Display hex_digit_display_18 (.value(R_2[7:4]));  // open: dp
  Hex_Digit_Display hex_digit_display_19 (.value(R_3[7:4]));  // open: dp
  Hex_Digit_Display hex_digit_display_20 (.value(ram_address[7:4]));  // open: dp
  Hex_Digit_Display hex_digit_display_21 (.value(RAMOUT[7:4]));  // open: dp
  Hex_Digit_Display hex_digit_display_22 (.value(address[3:0]));  // open: dp
  Hex_Digit_Display hex_digit_display_23 (.value(instruction[3:0]));  // open: dp
  Hex_Digit_Display hex_digit_display_24 (.value(R_1[3:0]));  // open: dp
  Hex_Digit_Display hex_digit_display_25 (.value(R_2[3:0]));  // open: dp
  Hex_Digit_Display hex_digit_display_26 (.value(R_3[3:0]));  // open: dp
  Hex_Digit_Display hex_digit_display_27 (.value(ram_address[3:0]));  // open: dp
  Hex_Digit_Display hex_digit_display_28 (.value(RAMOUT[3:0]));  // open: dp
  Hex_Digit_Display hex_digit_display_29 (.value(R_13[15:12]));  // open: dp
  Hex_Digit_Display hex_digit_display_30 (.value(R_13[11:8]));  // open: dp
  Hex_Digit_Display hex_digit_display_31 (.value(R_13[7:4]));  // open: dp
  Hex_Digit_Display hex_digit_display_32 (.value(R_13[3:0]));  // open: dp

  // Notes on the sheet:
  //   contents of rom_1 (hex, n*v repeats v):
  //   3160 e101 f1ff e216 f200 a312 d423 35c6 3645 e901 f9c0 6609 4709 3815
  //   Register Bank
  //   Main Module for HERA Processor
  //   RAM
  //   Flags (from left to right): Sign, Zero, Overflow, Carry, CarryBlock
  //   Flag Bank
  //   Address
  //   Instructions
  //   Register 1
  //   Register 2
  //   Register 3
  //   RAM Address
  //   RAM Output
  //   PC_ret
endmodule

// RegBank
module RegisterBank (
  input  [15:0] R_d,
  input  [15:0] Ra_in,
  input  [15:0] Rb_in,
  input  [15:0] FP_in,
  input  [3:0] d,
  input  [3:0] a,
  input  [3:0] b,
  input  [3:0] opcode,
  input  clk,
  output [15:0] R_1,
  output [15:0] R_2,
  output [15:0] R_3,
  output [15:0] R13_out,
  output [15:0] Ra_out,
  output [15:0] Rb_out,
  output [15:0] FP_out,
  output [15:0] R_b,
  output [15:0] R_a
);

  wire and_1_out, and_2_out, and_3_out, and_4_out, and_5_out, and_6_out, and_7_out, and_8_out, and_9_out,
       and_10_out, and_11_out, and_12_out, and_13_out, and_14_out, and_15_out, and_16_out, and_17_out,
       and_18_out, and_19_out, and_20_out, and_21_out, and_22_out, and_23_out, and_24_out, and_25_out,
       and_26_out, and_27_out, and_28_out, and_29_out, and_30_out, comparator_1_eq, comparator_2_eq,
       or_1_out, or_2_out, or_3_out, or_4_out, or_5_out, or_6_out, or_7_out, or_8_out, or_9_out, or_10_out,
       or_11_out, or_12_out, or_13_out, or_14_out, or_15_out, or_16_out, R0_in, R0_in_a, R0_in_b, R0_in_d,
       R1_in, R1_in_a, R1_in_b, R1_in_d, R2_in, R2_in_a, R2_in_b, R2_in_d, R3_in, R3_in_a, R3_in_b, R3_in_d,
       R4_in, R4_in_a, R4_in_b, R4_in_d, R5_in, R5_in_a, R5_in_b, R5_in_d, R6_in, R6_in_a, R6_in_b, R6_in_d,
       R7_in, R7_in_a, R7_in_b, R7_in_d, R8_in, R8_in_a, R8_in_b, R8_in_d, R9_in, R9_in_a, R9_in_b, R9_in_d,
       R10_in, R10_in_a, R10_in_b, R10_in_d, R11_in, R11_in_a, R11_in_b, R11_in_d, R12_in, R12_in_a,
       R12_in_b, R12_in_d, R13_in, R13_in_a, R13_in_b, R13_in_d, R14_in, R14_in_a, R14_in_b, R14_in_d,
       R15_in, R15_in_a, R15_in_b, R15_in_d;
  wire [15:0] multiplexer_14_out, multiplexer_15_out, multiplexer_16_out, multiplexer_17_out,
       multiplexer_26_out, multiplexer_27_out, multiplexer_28_out, multiplexer_29_out, multiplexer_38_out,
       multiplexer_39_out, multiplexer_40_out, multiplexer_41_out, multiplexer_49_out, multiplexer_51_out,
       multiplexer_52_out, multiplexer_55_out, R0_out, R1, R2, R3, R4, R4_out, R5, R5_out, R6, R6_out, R7,
       R7_out, R8, R8_out, R9, R9_out, R10, R10_out, R11, R11_out, R12, R13, R14, R15, R15_out;

  Decoder #(.select(4)) decoder_1 (
    .out0(R0_in_d), .out1(R1_in_d), .out2(R2_in_d), .out3(R3_in_d), .out4(R4_in_d), .out5(R5_in_d),
    .out6(R6_in_d), .out7(R7_in_d), .out8(R8_in_d), .out9(R9_in_d), .out10(R10_in_d), .out11(R11_in_d),
    .out12(R12_in_d), .out13(R13_in_d), .out14(R14_in_d), .out15(R15_in_d), .sel(d));  // open: en
  Comparator #(.width(4)) comparator_1 (.a(opcode), .b(4'b0010), .eq(comparator_1_eq));  // open: gt, lt
  Register #(.width(16)) R0 (.D({16{1'b0}}), .en(R0_in), .clk(clk), .Q(R0_out));  // open: clr
  Register #(.width(16)) u_R4 (.D(R4), .en(R4_in), .clk(clk), .Q(R4_out));  // open: clr
  Register #(.width(16)) u_R8 (.D(R8), .en(R8_in), .clk(clk), .Q(R8_out));  // open: clr
  Register #(.width(16)) u_R12 (.D(R12), .en(R12_in), .clk(clk), .Q(Ra_out));  // open: clr
  Multiplexer #(.width(16)) multiplexer_1 (.in0(R_d), .in1(Rb_in), .out(R13), .sel(comparator_1_eq));
  Register #(.width(16)) u_R1 (.D(R1), .en(R1_in), .clk(clk), .Q(R_1));  // open: clr
  Register #(.width(16)) u_R5 (.D(R5), .en(R5_in), .clk(clk), .Q(R5_out));  // open: clr
  Register #(.width(16)) u_R9 (.D(R9), .en(R9_in), .clk(clk), .Q(R9_out));  // open: clr
  Register #(.width(16)) u_R13 (.D(R13), .en(R13_in), .clk(clk), .Q(R13_out));  // open: clr
  Multiplexer #(.width(16)) multiplexer_2 (.in0(R_d), .in1(Ra_in), .out(R12), .sel(comparator_1_eq));
  Register #(.width(16)) u_R2 (.D(R2), .en(R2_in), .clk(clk), .Q(R_2));  // open: clr
  Register #(.width(16)) u_R6 (.D(R6), .en(R6_in), .clk(clk), .Q(R6_out));  // open: clr
  Register #(.width(16)) u_R10 (.D(R10), .en(R10_in), .clk(clk), .Q(R10_out));  // open: clr
  Register #(.width(16)) u_R14 (.D(R14), .en(R14_in), .clk(clk), .Q(FP_out));  // open: clr
  Multiplexer #(.select(4), .width(16)) multiplexer_3 (
    .in0(R0_out), .in1(R_1), .in2(R_2), .in3(R_3), .in4(R4_out), .in5(R5_out), .in6(R6_out), .in7(R7_out),
    .in8(R8_out), .in9(R9_out), .in10(R10_out), .in11(R11_out), .in12(Ra_out), .in13(R13_out), .in14(FP_out),
    .in15(R15_out), .out(R_a), .sel(a));
  Multiplexer #(.width(16)) multiplexer_4 (.in0(R_d), .in1(FP_in), .out(R14), .sel(comparator_1_eq));
  Register #(.width(16)) u_R3 (.D(R3), .en(R3_in), .clk(clk), .Q(R_3));  // open: clr
  Register #(.width(16)) u_R7 (.D(R7), .en(R7_in), .clk(clk), .Q(R7_out));  // open: clr
  Register #(.width(16)) u_R11 (.D(R11), .en(R11_in), .clk(clk), .Q(R11_out));  // open: clr
  Register #(.width(16)) u_R15 (.D(R15), .en(R15_in), .clk(clk), .Q(R15_out));  // open: clr
  Multiplexer multiplexer_5 (.in0(R14_in_d), .in1(1'b1), .out(R14_in), .sel(comparator_1_eq));
  Multiplexer #(.select(4), .width(16)) multiplexer_6 (
    .in0(R0_out), .in1(R_1), .in2(R_2), .in3(R_3), .in4(R4_out), .in5(R5_out), .in6(R6_out), .in7(R7_out),
    .in8(R8_out), .in9(R9_out), .in10(R10_out), .in11(R11_out), .in12(Ra_out), .in13(R13_out), .in14(FP_out),
    .in15(R15_out), .out(R_b), .sel(b));
  Multiplexer multiplexer_7 (.in0(R12_in_d), .in1(1'b1), .out(R12_in), .sel(comparator_1_eq));
  Decoder #(.select(4)) decoder_2 (
    .out0(R0_in_a), .out1(R1_in_a), .out2(R2_in_a), .out3(R3_in_a), .out4(R4_in_a), .out5(R5_in_a),
    .out6(R6_in_a), .out7(R7_in_a), .out8(R8_in_a), .out9(R9_in_a), .out10(R10_in_a), .out11(R11_in_a),
    .out12(R12_in_a), .out13(R13_in_a), .out14(R14_in_a), .out15(R15_in_a), .sel(a));  // open: en
  Multiplexer multiplexer_8 (.in0(R13_in_d), .in1(1'b1), .out(R13_in), .sel(comparator_1_eq));
  Decoder #(.select(4)) decoder_3 (
    .out0(R0_in_b), .out1(R1_in_b), .out2(R2_in_b), .out3(R3_in_b), .out4(R4_in_b), .out5(R5_in_b),
    .out6(R6_in_b), .out7(R7_in_b), .out8(R8_in_b), .out9(R9_in_b), .out10(R10_in_b), .out11(R11_in_b),
    .out12(R12_in_b), .out13(R13_in_b), .out14(R14_in_b), .out15(R15_in_b), .sel(b));  // open: en
  Multiplexer multiplexer_9 (.in0(R1_in_d), .in1(1'b0), .out(R1_in), .sel(comparator_1_eq));
  Comparator #(.width(4)) comparator_2 (.a(opcode), .b(4'b0010), .eq(comparator_2_eq));  // open: gt, lt
  or or_1 (or_1_out, R0_in_a, R0_in_b);
  or or_2 (or_2_out, R4_in_a, R4_in_b);
  or or_3 (or_3_out, R8_in_a, R8_in_b);
  or or_4 (or_4_out, R12_in_a, R12_in_b);
  and and_1 (and_1_out, R1_in_b, comparator_2_eq);
  and and_2 (and_2_out, R4_in_b, comparator_2_eq);
  and and_3 (and_3_out, R8_in_b, comparator_2_eq);
  and and_4 (and_4_out, R12_in_b, comparator_2_eq);
  Multiplexer multiplexer_10 (.in0(R0_in_d), .in1(or_1_out), .out(R0_in), .sel(comparator_2_eq));
  Multiplexer multiplexer_11 (.in0(R4_in_d), .in1(or_2_out), .out(R4_in), .sel(comparator_2_eq));
  Multiplexer multiplexer_12 (.in0(R8_in_d), .in1(or_3_out), .out(R8_in), .sel(comparator_2_eq));
  Multiplexer multiplexer_13 (.in0(R12_in_d), .in1(or_4_out), .out(R12_in), .sel(comparator_2_eq));
  Multiplexer #(.width(16)) multiplexer_14 (.in0(R_d), .in1(Rb_in), .out(multiplexer_14_out), .sel(and_1_out));
  Multiplexer #(.width(16)) multiplexer_15 (.in0(R_d), .in1(Rb_in), .out(multiplexer_15_out), .sel(and_2_out));
  Multiplexer #(.width(16)) multiplexer_16 (.in0(R_d), .in1(Rb_in), .out(multiplexer_16_out), .sel(and_3_out));
  Multiplexer #(.width(16)) multiplexer_17 (.in0(R_d), .in1(Rb_in), .out(multiplexer_17_out), .sel(and_4_out));
  and and_5 (and_5_out, R1_in_a, comparator_2_eq);
  and and_6 (and_6_out, R4_in_a, comparator_2_eq);
  and and_7 (and_7_out, R8_in_a, comparator_2_eq);
  and and_8 (and_8_out, R12_in_a, comparator_2_eq);
  Multiplexer #(.width(16)) multiplexer_18 (.in0(multiplexer_14_out), .in1(Ra_in), .out(R1), .sel(and_5_out));
  Multiplexer #(.width(16)) multiplexer_19 (.in0(multiplexer_15_out), .in1(Ra_in), .out(R4), .sel(and_6_out));
  Multiplexer #(.width(16)) multiplexer_20 (.in0(multiplexer_16_out), .in1(Ra_in), .out(R8), .sel(and_7_out));
  Multiplexer #(.width(16)) multiplexer_21 (.in0(multiplexer_17_out), .in1(Ra_in), .out(R12), .sel(and_8_out));
  or or_5 (or_5_out, R1_in_a, R1_in_b);
  or or_6 (or_6_out, R5_in_a, R5_in_b);
  or or_7 (or_7_out, R9_in_a, R9_in_b);
  or or_8 (or_8_out, R13_in_a, R13_in_b);
  Multiplexer multiplexer_22 (.in0(R1_in_d), .in1(or_5_out), .out(R1_in), .sel(comparator_2_eq));
  Multiplexer multiplexer_23 (.in0(R5_in_d), .in1(or_6_out), .out(R5_in), .sel(comparator_2_eq));
  Multiplexer multiplexer_24 (.in0(R9_in_d), .in1(or_7_out), .out(R9_in), .sel(comparator_2_eq));
  Multiplexer multiplexer_25 (.in0(R13_in_d), .in1(or_8_out), .out(R13_in), .sel(comparator_2_eq));
  and and_9 (and_9_out, R2_in_b, comparator_2_eq);
  and and_10 (and_10_out, R5_in_b, comparator_2_eq);
  and and_11 (and_11_out, R9_in_b, comparator_2_eq);
  and and_12 (and_12_out, R13_in_b, comparator_2_eq);
  Multiplexer #(.width(16)) multiplexer_26 (.in0(R_d), .in1(Rb_in), .out(multiplexer_26_out), .sel(and_9_out));
  Multiplexer #(.width(16)) multiplexer_27 (.in0(R_d), .in1(Rb_in), .out(multiplexer_27_out), .sel(and_10_out));
  Multiplexer #(.width(16)) multiplexer_28 (.in0(R_d), .in1(Rb_in), .out(multiplexer_28_out), .sel(and_11_out));
  Multiplexer #(.width(16)) multiplexer_29 (.in0(R_d), .in1(Rb_in), .out(multiplexer_29_out), .sel(and_12_out));
  and and_13 (and_13_out, R2_in_a, comparator_2_eq);
  and and_14 (and_14_out, R5_in_a, comparator_2_eq);
  and and_15 (and_15_out, R9_in_a, comparator_2_eq);
  and and_16 (and_16_out, R13_in_a, comparator_2_eq);
  Multiplexer multiplexer_30 (.in0(R2_in_d), .in1(or_9_out), .out(R2_in), .sel(comparator_2_eq));
  or or_9 (or_9_out, R2_in_a, R2_in_b);
  Multiplexer multiplexer_31 (.in0(R6_in_d), .in1(or_10_out), .out(R6_in), .sel(comparator_2_eq));
  or or_10 (or_10_out, R6_in_a, R6_in_b);
  Multiplexer multiplexer_32 (.in0(R10_in_d), .in1(or_11_out), .out(R10_in), .sel(comparator_2_eq));
  or or_11 (or_11_out, R10_in_a, R10_in_b);
  Multiplexer multiplexer_33 (.in0(R14_in_d), .in1(or_12_out), .out(R14_in), .sel(comparator_2_eq));
  or or_12 (or_12_out, R14_in_a, R14_in_b);
  Multiplexer #(.width(16)) multiplexer_34 (.in0(multiplexer_26_out), .in1(Ra_in), .out(R2), .sel(and_13_out));
  Multiplexer #(.width(16)) multiplexer_35 (.in0(multiplexer_27_out), .in1(Ra_in), .out(R5), .sel(and_14_out));
  Multiplexer #(.width(16)) multiplexer_36 (.in0(multiplexer_28_out), .in1(Ra_in), .out(R9), .sel(and_15_out));
  Multiplexer #(.width(16)) multiplexer_37 (.in0(multiplexer_29_out), .in1(Ra_in), .out(R13), .sel(and_16_out));
  Multiplexer #(.width(16)) multiplexer_38 (.in0(R_d), .in1(Rb_in), .out(multiplexer_38_out), .sel(and_17_out));
  and and_17 (and_17_out, R3_in_b, comparator_2_eq);
  Multiplexer #(.width(16)) multiplexer_39 (.in0(R_d), .in1(Rb_in), .out(multiplexer_39_out), .sel(and_18_out));
  and and_18 (and_18_out, R6_in_b, comparator_2_eq);
  Multiplexer #(.width(16)) multiplexer_40 (.in0(R_d), .in1(Rb_in), .out(multiplexer_40_out), .sel(and_19_out));
  and and_19 (and_19_out, R10_in_b, comparator_2_eq);
  Multiplexer #(.width(16)) multiplexer_41 (.in0(R_d), .in1(Rb_in), .out(multiplexer_41_out), .sel(and_20_out));
  and and_20 (and_20_out, R14_in_b, comparator_2_eq);
  or or_13 (or_13_out, R3_in_a, R3_in_b);
  or or_14 (or_14_out, R7_in_a, R7_in_b);
  or or_15 (or_15_out, R11_in_a, R11_in_b);
  or or_16 (or_16_out, R15_in_a, R15_in_b);
  Multiplexer multiplexer_42 (.in0(R3_in_d), .in1(or_13_out), .out(R3_in), .sel(comparator_2_eq));
  Multiplexer multiplexer_43 (.in0(R7_in_d), .in1(or_14_out), .out(R7_in), .sel(comparator_2_eq));
  Multiplexer multiplexer_44 (.in0(R11_in_d), .in1(or_15_out), .out(R11_in), .sel(comparator_2_eq));
  Multiplexer multiplexer_45 (.in0(R15_in_d), .in1(or_16_out), .out(R15_in), .sel(comparator_2_eq));
  Multiplexer #(.width(16)) multiplexer_46 (.in0(multiplexer_38_out), .in1(Ra_in), .out(R3), .sel(and_21_out));
  and and_21 (and_21_out, R3_in_a, comparator_2_eq);
  Multiplexer #(.width(16)) multiplexer_47 (.in0(multiplexer_39_out), .in1(Ra_in), .out(R6), .sel(and_22_out));
  and and_22 (and_22_out, R6_in_a, comparator_2_eq);
  Multiplexer #(.width(16)) multiplexer_48 (.in0(multiplexer_40_out), .in1(Ra_in), .out(R10), .sel(and_23_out));
  and and_23 (and_23_out, R10_in_a, comparator_2_eq);
  Multiplexer #(.width(16)) multiplexer_49 (
    .in0(multiplexer_41_out), .in1(Ra_in), .out(multiplexer_49_out), .sel(and_24_out));
  and and_24 (and_24_out, R14_in_a, comparator_2_eq);
  Multiplexer #(.width(16)) multiplexer_50 (.in0(multiplexer_49_out), .in1(FP_in), .out(R14), .sel(comparator_2_eq));
  Multiplexer #(.width(16)) multiplexer_51 (.in0(R_d), .in1(Rb_in), .out(multiplexer_51_out), .sel(and_25_out));
  and and_25 (and_25_out, R7_in_b, comparator_2_eq);
  Multiplexer #(.width(16)) multiplexer_52 (.in0(R_d), .in1(Rb_in), .out(multiplexer_52_out), .sel(and_26_out));
  and and_26 (and_26_out, R11_in_b, comparator_2_eq);
  and and_27 (and_27_out, R15_in_b, comparator_2_eq);
  Multiplexer #(.width(16)) multiplexer_53 (.in0(multiplexer_51_out), .in1(Ra_in), .out(R7), .sel(and_28_out));
  and and_28 (and_28_out, R7_in_a, comparator_2_eq);
  Multiplexer #(.width(16)) multiplexer_54 (.in0(multiplexer_52_out), .in1(Ra_in), .out(R11), .sel(and_29_out));
  and and_29 (and_29_out, R11_in_a, comparator_2_eq);
  Multiplexer #(.width(16)) multiplexer_55 (.in0(R_d), .in1(Rb_in), .out(multiplexer_55_out), .sel(and_27_out));
  and and_30 (and_30_out, R7_in_a, comparator_2_eq);
  Multiplexer #(.width(16)) multiplexer_56 (.in0(multiplexer_55_out), .in1(Ra_in), .out(R15), .sel(and_30_out));

  assign Rb_out = R13_out;

  // Other names for the same wires on the sheet: R1_out[15:0] = R_1; R2_out[15:0] = R_2; R3_out[15:0] = R_3;
  //   R12_out[15:0] = Ra_out; R14_out[15:0] = FP_out

  // Notes on the sheet:
  //   Register Bank
  //   Register bank containing 16 16-bit registers
  //   We can read two registers R_a and R_b and write to R_d
  //   CALL/RETURN require storing return address and caller's frame pointer in Rb and Ra
endmodule

// Reg_Bank
module Reg_Control (
  input  clk,
  input  [15:0] instruction,
  input  [15:0] Rd,
  input  [15:0] Ra_in,
  input  [15:0] Rb_in,
  input  [15:0] FP_in,
  output [15:0] R_1,
  output [15:0] R_2,
  output [15:0] R_3,
  output [15:0] R_13,
  output [15:0] FP_out,
  output [15:0] R_b,
  output [15:0] R_a
);

  wire and_1_out, and_2_out, and_3_out, comparator_1_eq, comparator_2_eq, comparator_3_eq, comparator_4_eq,
       comparator_4_gt, or_1_out, or_2_out;
  wire [3:0] d_final, multiplexer_1_out, multiplexer_3_out;
  wire [15:0] registerbank_1_ra_out;

  RegisterBank registerbank_1 (
    .R_d(Rd), .Ra_in(Ra_in), .Rb_in(Rb_in), .FP_in(FP_in), .d(d_final), .a(multiplexer_3_out),
    .b(instruction[3:0]), .opcode(instruction[15:12]), .clk(clk), .R_1(R_1), .R_2(R_2), .R_3(R_3),
    .R13_out(R_13), .Ra_out(registerbank_1_ra_out), .FP_out(FP_out), .R_b(R_b), .R_a(R_a));  // open: Rb_out
  Comparator #(.width(3)) comparator_1 (.a(instruction[15:13]), .b(3'b011), .eq(comparator_1_eq));  // open: gt, lt
  Comparator #(.width(3)) comparator_2 (.a(instruction[14:12]), .b(3'b011), .eq(comparator_2_eq));  // open: gt, lt
  Multiplexer #(.width(4)) multiplexer_1 (
    .in0(instruction[11:8]), .in1(4'b0000), .out(multiplexer_1_out), .sel(comparator_1_eq));
  and and_1 (and_1_out, comparator_2_eq, ~instruction[15]);  // AND_Gate
  or or_1 (or_1_out, comparator_1_eq, and_1_out);
  Multiplexer #(.select(4), .width(4)) multiplexer_2 (
    .in0(4'b0000), .in1(4'b0000), .in2(multiplexer_1_out), .in3(instruction[11:8]), .in4(instruction[11:8]),
    .in5(instruction[11:8]), .in6(instruction[11:8]), .in7(instruction[11:8]), .in8(instruction[11:8]),
    .in9(instruction[11:8]), .in10(instruction[11:8]), .in11(instruction[11:8]), .in12(instruction[11:8]),
    .in13(instruction[11:8]), .in14(instruction[11:8]), .in15(instruction[11:8]), .out(d_final),
    .sel(instruction[15:12]));
  Comparator #(.width(4)) comparator_3 (.a(instruction[7:4]), .b(4'b0111), .eq(comparator_3_eq));  // open: gt, lt
  and and_2 (and_2_out, comparator_4_gt, or_1_out);
  Comparator #(.width(2)) comparator_4 (
    .a(instruction[7:6]), .b(2'b10), .gt(comparator_4_gt), .eq(comparator_4_eq));  // open: lt
  and and_3 (and_3_out, comparator_4_eq, or_1_out);
  or or_2 (or_2_out, comparator_3_eq, and_2_out, and_3_out);
  Multiplexer #(.width(4)) multiplexer_3 (
    .in0(instruction[7:4]), .in1(instruction[11:8]), .out(multiplexer_3_out), .sel(or_2_out));

  // Other names for the same wires on the sheet: b[3:0] = instruction[3:0]; a[3:0] = instruction[7:4];
  //   d[3:0] = instruction[11:8]; opcode[3:0] = instruction[15:12]; R_d[15:0] = Rd

  // Notes on the sheet:
  //   Register Control
  //   We don't want to overwrite registers with STORE intruction
  //   Depending on instruction, we determine which value gets stored in a given address 
  //   3:0
  //   7:4
  //   11:8
  //   15:12
  //   inc/dec and restrf we save R_d as R_a
  //   We want to pass d into a when saving flags to R_d
endmodule

module ALSU (
  input  [4:0] Flags,
  input  [15:0] PC_in,
  input  [15:0] R_a,
  input  [15:0] R_b,
  input  [15:0] Rd,
  input  [15:0] FP,
  input  [15:0] instruction,
  input  [15:0] RAM_out,
  output [15:0] R_d,
  output [15:0] PC_out,
  output [15:0] Rb_out,
  output [15:0] Ra_out,
  output [15:0] FP_out,
  output enable,
  output [4:0] Flags_out
);

  wire BR, call_return_1_call_ret;
  wire [4:0] F_arith, F_bitwise, F_inc_dec, F_RAM, F_set, F_Shift, multiplexer_4_out, multiplexer_5_out;
  wire [15:0] arith, branch_1_pc_out, bw, call_return_1_pc_out, I_D, multiplexer_1_out, multiplexer_2_out,
       setlo, Shift;

  assign setlo = {{8{instruction[7]}}, instruction[7:0]};  // Bit_Extender bit_extender_1
  Bitwise bitwise_1 (.R_a(R_a), .R_b(R_b), .op(instruction[14:12]), .Flags_in(Flags), .R_d(bw), .Flags_out(F_bitwise));
  Arithmetic arithmetic_1 (
    .R_a(R_a), .R_b(R_b), .op(instruction[14:12]), .Flags_in(Flags), .R_d(arith), .Flags_out(F_arith));
  RAM_LOAD ram_load_1 (.RAM_out(RAM_out), .Flags_in(Flags), .Flags_out(F_RAM));
  Multiplexer #(.width(16)) multiplexer_1 (
    .in0({Rd[15:5], Flags}), .in1(R_a), .out(multiplexer_1_out), .sel(instruction[3]));
  LS ls_1 (.R_b_in(R_b), .op(instruction[6:4]), .Flags_in(Flags), .R_b_out(Shift), .Flags_out(F_Shift));
  INC_DEC inc_dec_1 (
    .R_d(R_a), .epsilon(instruction[5:0]), .op(instruction[6]), .Flags_in(Flags), .res(I_D),
    .Flags_out(F_inc_dec));
  Multiplexer #(.select(4), .width(16)) multiplexer_2 (
    .in0(Shift), .in1(Shift), .in2(Shift), .in3(Shift), .in4(Shift), .in5(Shift), .in6({16{1'b0}}),
    .in7(multiplexer_1_out), .in8(I_D), .in9(I_D), .in10(I_D), .in11(I_D), .in12(I_D), .in13(I_D),
    .in14(I_D), .in15(I_D), .out(multiplexer_2_out), .sel(instruction[7:4]));
  Flag_Set flag_set_1 (
    .opcode(instruction[11:9]), .Fin_instruction({instruction[8], instruction[3:0]}), .Flags_in(Flags),
    .Flags_out(F_set));
  Multiplexer #(.select(4), .width(16)) multiplexer_3 (
    .in0(R_b), .in1(R_b), .in2({16{1'b0}}), .in3(multiplexer_2_out), .in4(RAM_out), .in5(RAM_out), .in6(R_a),
    .in7({16{1'b0}}), .in8(bw), .in9(bw), .in10(arith), .in11(arith), .in12(arith), .in13(bw), .in14(setlo),
    .in15({instruction[7:0], Rd[7:0]}), .out(R_d), .sel(instruction[15:12]));
  Multiplexer #(.width(5)) multiplexer_4 (.in0(Flags), .in1(R_a[4:0]), .out(multiplexer_4_out), .sel(instruction[3]));
  Multiplexer #(.select(4), .width(5)) multiplexer_5 (
    .in0(F_Shift), .in1(F_Shift), .in2(F_Shift), .in3(F_Shift), .in4(F_Shift), .in5(F_Shift), .in6(F_set),
    .in7(multiplexer_4_out), .in8(F_inc_dec), .in9(F_inc_dec), .in10(F_inc_dec), .in11(F_inc_dec),
    .in12(F_inc_dec), .in13(F_inc_dec), .in14(F_inc_dec), .in15(F_inc_dec), .out(multiplexer_5_out),
    .sel(instruction[7:4]));
  Branch branch_1 (
    .PC_in(PC_in), .R_b(R_b), .flags(Flags), .a(instruction[7:4]), .b(instruction[3:0]),
    .d(instruction[11:8]), .in_7(instruction[15:12]), .PC_out(branch_1_pc_out), .br(BR));
  Call_Return call_return_1 (
    .PC_in(PC_in), .Rb(R_b), .Ra(R_a), .FP(FP), .opcode(instruction[15:12]), .PC_out(call_return_1_pc_out),
    .Rb_out(Rb_out), .Ra_out(Ra_out), .FP_out(FP_out), .call_ret(call_return_1_call_ret));
  Multiplexer #(.select(4), .width(5)) multiplexer_6 (
    .in0(Flags), .in1(Flags), .in2(Flags), .in3(multiplexer_5_out), .in4(F_RAM), .in5(F_RAM), .in6(Flags),
    .in7(Flags), .in8(F_bitwise), .in9(F_bitwise), .in10(F_arith), .in11(F_arith), .in12(F_arith),
    .in13(F_bitwise), .in14(Flags), .in15(Flags), .out(Flags_out), .sel(instruction[15:12]));
  or or_1 (enable, call_return_1_call_ret, BR);
  Multiplexer #(.select(4), .width(16)) multiplexer_7 (
    .in0(branch_1_pc_out), .in1(branch_1_pc_out), .in2(call_return_1_pc_out), .in3({16{1'b0}}),
    .in4({16{1'b0}}), .in5({16{1'b0}}), .in6({16{1'b0}}), .in7({16{1'b0}}), .in8({16{1'b0}}),
    .in9({16{1'b0}}), .in10({16{1'b0}}), .in11({16{1'b0}}), .in12({16{1'b0}}), .in13({16{1'b0}}),
    .in14({16{1'b0}}), .in15({16{1'b0}}), .out(PC_out), .sel(instruction[15:12]));

  // Other names for the same wires on the sheet: F[4:0] = Flags; sethi[15:0] = {instruction[7:0], Rd[7:0]};
  //   b[3:0] = instruction[3:0]; a[3:0] = instruction[7:4]; d[3:0] = instruction[11:8]; FP_in[15:0] = FP;
  //   opcode[3:0] = instruction[15:12]; RAM[15:0] = RAM_out

  // Notes on the sheet:
  //   ALSU
  //   SET instructions (SETLO, SETHI)
  //   Bitwise instructions (AND, OR, XOR)
  //   Arithmetic instructions (ADD, SUB, MUL)
  //   3:0
  //   7:4
  //   11:8
  //   15:12
  //   SAVEF
  //   Flag Instructions
  //   Flag opcode
  //   Input Flags
  //   Module that handles arithmetic and other operations done on values stored in register bank
  //   Manually setting flags (FON, FOFF, FSET4, FSET5)
  //   Shift Instructions (LSL, LSR, LSL8, LSR8, ASL, ASR)
  //   Increment and Decrement Instructions (INC, DEC)
  //   RESTRF
  //   Branch Instructions (BR, BL, etc.)
endmodule

module Call_Return (
  input  [15:0] PC_in,
  input  [15:0] Rb,
  input  [15:0] Ra,
  input  [15:0] FP,
  input  [3:0] opcode,
  output [15:0] PC_out,
  output [15:0] Rb_out,
  output [15:0] Ra_out,
  output [15:0] FP_out,
  output call_ret
);

  Adder #(.width(16)) adder_1 (.a(PC_in), .b(16'h1), .out(Rb_out));  // open: cin, cout
  Comparator #(.width(4)) comparator_1 (.a(opcode), .b(4'b0010), .eq(call_ret));  // open: gt, lt

  assign FP_out = Ra;
  assign PC_out = Rb;
  assign Ra_out = FP;

  // Other names for the same wires on the sheet: PC_out_t[15:0] = PC_in

  // Notes on the sheet:
  //   CALL/RETURN Module
endmodule

module Branch (
  input  [15:0] PC_in,
  input  [15:0] R_b,
  input  [4:0] flags,
  input  [3:0] a,
  input  [3:0] b,
  input  [3:0] d,
  input  [3:0] in_7,
  output [15:0] PC_out,
  output br
);

  wire BG, BGE, BL, BLE, BUG, BULE, comparator_1_eq, comparator_2_eq, cond, not_1_out, not_2_out, not_3_out,
       not_4_out, or_3_out, xor_2_out, xor_3_out;
  wire [15:0] bit_extender_1_out, REL;

  assign bit_extender_1_out = {{8{1'b0}}, {a, b}};  // Bit_Extender bit_extender_1
  Adder #(.width(16)) adder_1 (.a(bit_extender_1_out), .b(PC_in), .out(REL));  // open: cin, cout
  Multiplexer #(.width(16)) multiplexer_1 (.in0(REL), .in1(R_b), .out(PC_out), .sel(in_7[0]));
  xor xor_1 (BL, flags[0], flags[2]);
  xor xor_2 (xor_2_out, flags[0], flags[2]);
  or or_1 (BLE, xor_2_out, flags[1]);
  or or_2 (BULE, ~flags[3], flags[1]);  // OR_Gate
  nor nor_1 (BUG, ~flags[3], flags[1]);  // NOR_Gate
  Comparator #(.width(4)) comparator_1 (.a(in_7), .b(4'b0000), .eq(comparator_1_eq));  // open: gt, lt
  Comparator #(.width(4)) comparator_2 (.a(in_7), .b(4'b0001), .eq(comparator_2_eq));  // open: gt, lt
  Comparator #(.width(4)) comparator_3 ();  // open: a, b, gt, eq, lt
  xor xor_3 (xor_3_out, flags[0], flags[2]);
  xnor xnor_1 (BGE, flags[0], flags[2]);
  or or_3 (or_3_out, comparator_1_eq, comparator_2_eq);
  nor nor_2 (BG, xor_3_out, flags[1]);
  and and_1 (br, or_3_out, cond);
  not not_1 (not_1_out, flags[1]);
  not not_2 (not_2_out, flags[3]);
  not not_3 (not_3_out, flags[0]);
  not not_4 (not_4_out, flags[2]);
  Multiplexer #(.select(4)) multiplexer_2 (
    .in0(1'b1), .in2(BL), .in3(BGE), .in4(BLE), .in5(BG), .in6(BULE), .in7(BUG), .in8(flags[1]),
    .in9(not_1_out), .in10(flags[3]), .in11(not_2_out), .in12(flags[0]), .in13(not_3_out), .in14(flags[2]),
    .in15(not_4_out), .out(cond), .sel(d));  // open: in1

  // Other names for the same wires on the sheet: s = flags[0]; z = flags[1]; v = flags[2]; c = flags[3];
  //   cb = flags[4]; opcode[3:0] = in_7; rel_t = in_7[0]

  // Notes on the sheet:
  //   Register-Mode and Relative Branch Instructions
  //   Register-Mode Branch Instructions
endmodule

module PC (
  input  clk,
  input  [15:0] PC_out,
  input  BR,
  output [15:0] addresss
);

  Counter #(.max('hffff), .width(16)) counter_1 (
    .load(BR), .D(PC_out), .Q(addresss), .clk(clk));  // open: count, carry, up, clr

  // Other names for the same wires on the sheet: addr[15:0] = addresss; BR_reg = BR; R_d[15:0] = PC_out

  // Notes on the sheet:
  //   Program counter:  
  //   We read through four bit addresses that are fed into our ROM to retrieve instructions for the CPU. 
  //   Loading the ROM addresss directly froom a register <- branching
  //   Relative branching replaces current ROM address with the current address plus an offset: PC_i+1 <= PC_i + o
  //   PC <= R_b
endmodule

// Flags
module FlagBank (
  input  clk,
  input  [4:0] flags,
  output [4:0] flags_out
);

  wire reset;

  D_Flip_Flop Sign (.D(flags[0]), .clk(clk), .Q(flags_out[0]), .reset(reset));  // open: Qn, preset
  D_Flip_Flop Carry (.D(flags[3]), .clk(clk), .Q(flags_out[3]), .reset(reset));  // open: Qn, preset
  D_Flip_Flop Zero (.D(flags[1]), .clk(clk), .Q(flags_out[1]), .reset(reset));  // open: Qn, preset
  D_Flip_Flop Carryblock (.D(flags[4]), .clk(clk), .Q(flags_out[4]), .reset(reset));  // open: Qn, preset
  D_Flip_Flop Overflow (.D(flags[2]), .clk(clk), .Q(flags_out[2]), .reset(reset));  // open: Qn, preset

  // Other names for the same wires on the sheet: F0 = flags[0]; F1 = flags[1]; F2 = flags[2]; F3 = flags[3];
  //   F4 = flags[4]; F0_out = flags_out[0]; F1_out = flags_out[1]; F2_out = flags_out[2]; F3_out = flags_out[3];
  //   F4_out = flags_out[4]

  // Notes on the sheet:
  //   Flag bank: consists of five D-flip flops to store the current state of each flag
endmodule

// F_Set
module Flag_Set (
  input  [2:0] opcode,
  input  [4:0] Fin_instruction,
  input  [4:0] Flags_in,
  output [4:0] Flags_out
);

  wire [4:0] FOFF, FON;

  assign FON = Fin_instruction | Flags_in;  // OR_Gate or_1, 5 bits wide
  assign FOFF = Flags_in & ~Fin_instruction;  // AND_Gate and_1, 5 bits wide
  Multiplexer #(.select(3), .width(5)) multiplexer_1 (
    .in0(FON), .in1(Flags_in), .in2(Fin_instruction), .in3(Flags_in), .in4(FOFF), .in5(Flags_in),
    .in6({Flags_in[4], Fin_instruction[3:0]}), .in7(Flags_in), .out(Flags_out), .sel(opcode));

  // Other names for the same wires on the sheet: FSET4[4:0] = {Flags_in[4], Fin_instruction[3:0]};
  //   FSET5[4:0] = Fin_instruction; cb_flag = Flags_in[4]

  // Notes on the sheet:
  //   Manually Setting Flags
  //   Given the instructions, we can manually turn on and off flags.
  //   FSET4 leaves carry block flag unchanged 
endmodule

module LS (
  input  [15:0] R_b_in,
  input  [2:0] op,
  input  [4:0] Flags_in,
  output [15:0] R_b_out,
  output [4:0] Flags_out
);

  wire and_1_out, and_2_out, and_3_out, and_4_out, comparator_2_eq, decoder_1_out0, decoder_1_out1,
       decoder_1_out4, decoder_1_out5, h, or_1_out, or_2_out, xor_1_out;
  wire [14:0] LSL;
  wire [15:0] LeftShift, LSL8, LSR, LSR8, RightShift;

  Decoder #(.select(3)) decoder_1 (
    .out0(decoder_1_out0), .out1(decoder_1_out1), .out4(decoder_1_out4), .out5(decoder_1_out5), .sel(op));  // open: out2, out3, out6, out7, en
  Comparator #(.width(16)) comparator_1 (
    .a(R_b_out), .b({16{1'b0}}), .eq(Flags_out[1]), .lt(Flags_out[0]));  // open: gt
  or or_1 (or_1_out, decoder_1_out0, decoder_1_out4);
  or or_2 (or_2_out, decoder_1_out1, decoder_1_out5);
  Shifter #(.width(16)) shifter_1 (.in(R_b_in), .\dist (4'b0001), .out({h, LSL}));
  Shifter #(.shift("lr"), .width(16)) shifter_2 (.in(R_b_in), .\dist (4'b0001), .out(LSR));
  Shifter #(.width(16)) shifter_3 (.in(R_b_in), .\dist (4'b1000), .out(LSL8));
  Shifter #(.shift("lr"), .width(16)) shifter_4 (.in(R_b_in), .\dist (4'b1000), .out(LSR8));
  and and_1 (and_1_out, R_b_in[15], or_1_out);
  and and_2 (and_2_out, R_b_in[0], or_2_out);
  or or_3 (Flags_out[3], and_1_out, and_2_out);
  Multiplexer #(.select(3), .width(16)) multiplexer_1 (
    .in0(LeftShift), .in1(RightShift), .in2(LSL8), .in3(LSR8), .in4(LeftShift),
    .in5({R_b_in[15], LSR[14:0]}), .in6({16{1'b0}}), .in7({16{1'b0}}), .out(R_b_out), .sel(op));
  and and_3 (and_3_out, ~Flags_in[4], Flags_in[3]);  // AND_Gate
  and and_4 (and_4_out, ~Flags_in[4], Flags_in[3]);  // AND_Gate
  Multiplexer #(.width(16)) multiplexer_2 (
    .in0({h, LSL}), .in1({h, LSL[14:1], Flags_in[3]}), .out(LeftShift), .sel(and_3_out));
  Multiplexer #(.width(16)) multiplexer_3 (
    .in0(LSR), .in1({Flags_in[3], LSR[15:1]}), .out(RightShift), .sel(and_4_out));
  xor xor_1 (xor_1_out, h, R_b_in[15]);
  Comparator #(.width(3)) comparator_2 (.a(op), .b(3'b100), .eq(comparator_2_eq));  // open: gt, lt
  Multiplexer multiplexer_4 (.in0(1'b0), .in1(xor_1_out), .out(Flags_out[2]), .sel(comparator_2_eq));

  assign Flags_out[4] = Flags_in[4];

  // Other names for the same wires on the sheet: high = R_b_in[15]; Rb[15:0] = R_b_in; LSL[15] = h; C = Flags_in[3];
  //   v = Flags_out[2]; CB = Flags_in[4]; R_b[15:0] = R_b_out; low = R_b_in[0]

  // Notes on the sheet:
  //   Logical Shift Operations
  //   Module for performing various logical shift operations on the value stored in a given register 
  //   Logical Shift Left
  //   Logical Shift Right
  //   Logical Shift Left 8-bits
  //   Logical Shift Right 8-bits
  //   check if bit is 1 on far left or right: if yes then depending on whether its a logical shift right or left then turn on carry flag 
  //   For LSR
  //   For LSL and ASL
  //   overflow flag set for ASL
endmodule

// INC/DEC
module INC_DEC (
  input  [15:0] R_d,
  input  [5:0] epsilon,
  input  op,
  input  [4:0] Flags_in,
  output [15:0] res,
  output [4:0] Flags_out
);

  wire c14;
  wire [1:0] c_add, c_sub;
  wire [5:0] adder_1_out, adder_2_out;
  wire [15:0] bit_extender_1_out, bit_extender_2_out, dec, inc, not_1_out;

  Adder #(.width(6)) adder_1 (.a(epsilon), .b(6'b000001), .out(adder_1_out));  // open: cin, cout
  Adder #(.width(6)) adder_2 (.a(epsilon), .b(6'b000001), .out(adder_2_out));  // open: cin, cout
  assign bit_extender_1_out = {{10{adder_1_out[5]}}, adder_1_out};  // Bit_Extender bit_extender_1
  assign bit_extender_2_out = {{10{adder_2_out[5]}}, adder_2_out};  // Bit_Extender bit_extender_2
  assign not_1_out = ~bit_extender_1_out;  // NOT_Gate not_1, 16 bits wide
  xor xor_1 (Flags_out[2], Flags_out[3], c14);
  ADD add_1 (.c_in(1'b0), .R_a(R_d), .R_b(bit_extender_2_out), .sum(inc), .c_out(c_add));
  ADD add_2 (.c_in(1'b1), .R_a(R_d), .R_b(not_1_out), .sum(dec), .c_out(c_sub));
  Multiplexer #(.width(16)) multiplexer_1 (.in0(inc), .in1(dec), .out({Flags_out[0], res[14:0]}), .sel(op));
  Multiplexer #(.width(2)) multiplexer_2 (.in0(c_add), .in1(c_sub), .out({Flags_out[3], c14}), .sel(op));
  Comparator #(.width(16)) comparator_1 (
    .a({Flags_out[0], res[14:0]}), .b({16{1'b0}}), .eq(Flags_out[1]));  // open: gt, lt

  assign Flags_out[4] = Flags_in[4];
  assign res[15] = Flags_out[0];

  // Other names for the same wires on the sheet: c15 = Flags_out[3]; F_in[4:0] = Flags_in; z = Flags_out[1];
  //   s = Flags_out[0]

  // Notes on the sheet:
  //   Increment/Decrement
endmodule

module Bitwise (
  input  [15:0] R_a,
  input  [15:0] R_b,
  input  [2:0] op,
  input  [4:0] Flags_in,
  output [15:0] R_d,
  output [4:0] Flags_out
);

  wire [15:0] AND, OR, XOR;

  assign AND = R_a & R_b;  // AND_Gate AND, 16 bits wide
  assign OR = R_a | R_b;  // OR_Gate OR, 16 bits wide
  assign XOR = R_a ^ R_b;  // XOR_Gate XOR, 16 bits wide
  Multiplexer #(.select(3), .width(16)) multiplexer_1 (
    .in0(AND), .in1(OR), .in5(XOR), .out({Flags_out[0], R_d[14:0]}), .sel(op));  // open: in2, in3, in4, in6, in7
  Comparator #(.width(16)) comparator_1 (
    .a({Flags_out[0], R_d[14:0]}), .b({16{1'b0}}), .eq(Flags_out[1]));  // open: gt, lt

  assign Flags_out[4:2] = Flags_in[4:2];
  assign R_d[15] = Flags_out[0];

  // Other names for the same wires on the sheet: z = Flags_out[1]; s = Flags_out[0]

  // Notes on the sheet:
  //   Bitwise instructions 
  //   AND logic
  //   OR logic
  //   XOR logic
  //   set s to B_15 of the result
endmodule

module Arithmetic (
  input  [15:0] R_a,
  input  [15:0] R_b,
  input  [2:0] op,
  input  [4:0] Flags_in,
  output [15:0] R_d,
  output [4:0] Flags_out
);

  wire and_1_out, and_2_out, c14, comparator_1_gt, comparator_1_lt, comparator_2_eq, not_3_out, or_1_out,
       xor_1_out, xor_2_out;
  wire [1:0] bit_extender_2_out, c_add, c_add_cboff, c_add_cbon, c_sub, c_sub_cboff, c_sub_cbon;
  wire [15:0] A, A_cboff, A_cbon, L_MUL, MUL, not_1_out, not_2_out, SUB, SUB_cboff, SUB_cbon, U_MUL;
  wire [31:0] bit_extender_1_out;

  assign not_1_out = ~R_b;  // NOT_Gate not_1, 16 bits wide
  assign not_2_out = ~R_b;  // NOT_Gate not_2, 16 bits wide
  ADD add_1 (.c_in(1'b0), .R_a(R_a), .R_b(R_b), .sum(A_cbon), .c_out(c_add_cbon));
  ADD add_2 (.c_in(1'b1), .R_a(R_a), .R_b(R_b), .sum(A_cboff), .c_out(c_add_cboff));
  ADD add_3 (.c_in(1'b1), .R_a(R_a), .R_b(not_1_out), .sum(SUB_cbon), .c_out(c_sub_cbon));
  ADD add_4 (.c_in(1'b0), .R_a(R_a), .R_b(not_2_out), .sum(SUB_cboff), .c_out(c_sub_cboff));
  Multiplier #(.width(16)) multiplier_1 (.a(R_a), .b(R_b), .out(L_MUL), .cout(U_MUL));  // open: cin
  Multiplexer #(.width(16)) multiplexer_1 (.in0(A_cboff), .in1(A_cbon), .out(A), .sel(Flags_in[4]));
  Multiplexer #(.width(2)) multiplexer_2 (.in0(c_add_cboff), .in1(c_add_cbon), .out(c_add), .sel(Flags_in[4]));
  Multiplexer #(.width(16)) multiplexer_3 (.in0(SUB_cboff), .in1(SUB_cbon), .out(SUB), .sel(Flags_in[4]));
  Multiplexer #(.width(2)) multiplexer_4 (.in0(c_sub_cboff), .in1(c_sub_cbon), .out(c_sub), .sel(Flags_in[4]));
  Multiplexer #(.width(16)) multiplexer_5 (.in0(L_MUL), .in1(U_MUL), .out(MUL), .sel(and_1_out));
  and and_1 (and_1_out, Flags_in[0], ~Flags_in[4]);  // AND_Gate
  or or_1 (or_1_out, comparator_1_gt, comparator_1_lt);
  Comparator #(.width(16)) comparator_1 (
    .a(U_MUL), .b({16{1'b0}}), .gt(comparator_1_gt), .lt(comparator_1_lt));  // open: eq
  assign bit_extender_1_out = {{15{Flags_out[0]}}, {Flags_out[0], L_MUL}};  // Bit_Extender bit_extender_1
  assign bit_extender_2_out = {{1{or_1_out}}, or_1_out};  // Bit_Extender bit_extender_2
  xor xor_1 (xor_1_out, Flags_out[3], c14);
  Multiplexer #(.select(3), .width(16)) multiplexer_6 (
    .in0({16{1'b0}}), .in1({16{1'b0}}), .in2(A), .in3(SUB), .in4(MUL), .in5({16{1'b0}}), .in6({16{1'b0}}),
    .in7({16{1'b0}}), .out({Flags_out[0], R_d[14:0]}), .sel(op));
  Multiplexer #(.select(3)) multiplexer_7 (
    .in0(1'b0), .in1(1'b0), .in2(xor_1_out), .in3(xor_1_out), .in4(xor_2_out), .in5(1'b0), .in6(1'b0),
    .in7(1'b0), .out(Flags_out[2]), .sel(op));
  Comparator #(.width(32)) comparator_2 (
    .a({U_MUL, L_MUL}), .b(bit_extender_1_out), .eq(comparator_2_eq));  // open: gt, lt
  Comparator #(.width(16)) comparator_3 (
    .a({Flags_out[0], R_d[14:0]}), .b({16{1'b0}}), .eq(Flags_out[1]));  // open: gt, lt
  Multiplexer #(.select(3), .width(2)) multiplexer_8 (
    .in0(2'b00), .in1(2'b00), .in2(c_add), .in3(c_sub), .in4(bit_extender_2_out), .in5(2'b00), .in6(2'b00),
    .in7(2'b00), .out({Flags_out[3], c14}), .sel(op));
  xor xor_2 (xor_2_out, not_3_out, and_2_out);
  not not_3 (not_3_out, comparator_2_eq);
  and and_2 (and_2_out, Flags_in[0], ~Flags_in[4]);  // AND_Gate

  assign Flags_out[4] = Flags_in[4];
  assign R_d[15] = Flags_out[0];

  // Other names for the same wires on the sheet: F_in[4:0] = Flags_in; s_init = Flags_in[0]; s = Flags_out[0];
  //   z = Flags_out[1]; c15 = Flags_out[3]; CB_flag = Flags_in[4]; SUB_013[13:0] = SUB[13:0]; SUB_14 = SUB[14];
  //   SUB_15 = SUB[15]

  // Notes on the sheet:
  //   ADD logic
  //   SUB logic
  //   MUL logic
  //   Arithmetic Instructions (ADD, SUB, MUL)
  //   Perform arithmetic operations depending on CB flag
  //   sign extend lower 16 bits of MUL
  //   Flag setting for arithmetic operations
endmodule

module ADD (
  input  c_in,
  input  [15:0] R_a,
  input  [15:0] R_b,
  output [15:0] sum,
  output [1:0] c_out
);

  wire adder_1_cout;

  Adder #(.width(14)) adder_1 (.a(R_a[13:0]), .b(R_b[13:0]), .out(sum[13:0]), .cin(c_in), .cout(adder_1_cout));
  Adder #(.width(1)) adder_2 (.a(R_a[14]), .b(R_b[14]), .out(sum[14]), .cin(adder_1_cout), .cout(c_out[0]));
  Adder #(.width(1)) adder_3 (.a(R_a[15]), .b(R_b[15]), .out(sum[15]), .cin(c_out[0]), .cout(c_out[1]));

  // Other names for the same wires on the sheet: ADD_13[13:0] = sum[13:0]; ADD_14 = sum[14]; ADD_15 = sum[15]

  // Notes on the sheet:
  //   Carry In
  //   Add Module: Peforms addition and subtraction on R_a and R_b
  //   Carry Out
endmodule

// RAM OUT
module RAM_LOAD (
  input  [15:0] RAM_out,
  input  [4:0] Flags_in,
  output [4:0] Flags_out
);

  Comparator #(.width(16)) comparator_1 (.a(RAM_out), .b({16{1'b0}}), .eq(Flags_out[1]));  // open: gt, lt

  assign {Flags_out[4:2], Flags_out[0]} = {Flags_in[4:2], RAM_out[15]};

  // Other names for the same wires on the sheet: s = RAM_out[15]; z = Flags_out[1]

  // Notes on the sheet:
  //   RAM_LOAD: Processes value loaded from RAM through ALSU
  //   Flag setting for RAM output
endmodule

// RAM Instructions
module RAM_Instructions (
  input  [15:0] R_b,
  input  [15:0] instruction,
  output [15:0] Address,
  output LD,
  output ST
);

  wire [15:0] adder_1_out, bit_extender_1_out, multiplexer_1_out, multiplexer_2_out;

  assign bit_extender_1_out = {{11{instruction[12]}}, {instruction[12], instruction[7:4]}};  // Bit_Extender bit_extender_1
  and and_1 (LD, ~instruction[13], instruction[14], ~instruction[15]);  // AND_Gate
  and and_2 (ST, instruction[13], instruction[14], ~instruction[15]);  // AND_Gate
  Adder #(.width(16)) adder_1 (.a(R_b), .b(bit_extender_1_out), .out(adder_1_out));  // open: cin, cout
  Multiplexer #(.width(16)) multiplexer_1 (.in0({16{1'b0}}), .in1(adder_1_out), .out(multiplexer_1_out), .sel(LD));
  Multiplexer #(.width(16)) multiplexer_2 (.in0({16{1'b0}}), .in1(adder_1_out), .out(multiplexer_2_out), .sel(ST));
  assign Address = multiplexer_1_out ^ multiplexer_2_out;  // XOR_Gate xor_1, 16 bits wide

  // Other names for the same wires on the sheet: a[3:0] = instruction[7:4]; opcode[3:0] = instruction[15:12];
  //   b[3:0] = instruction[3:0]; d[3:0] = instruction[11:8]

  // Notes on the sheet:
  //   RAM Instructions
  //   Processes the instructions for storing to or loading from RAM 
  //   3:0
  //   7:4
  //   11:8
  //   15:12
endmodule
